# Fritzing sketch solenoid_valve_circuit (saved by Fritzing 0.9.4)
breadboards: 1

parts:
  Part1 = Arduino Uno (Rev3)
  Q1 = TIP120 Hi-Current Darlington Transistor
  Q2 = TIP120 Hi-Current Darlington Transistor
  Q3 = TIP120 Hi-Current Darlington Transistor
  R1 = Resistor [tolerance=±5% resistance=220 package=THT]
  R2 = Resistor [tolerance=±5% resistance=220 package="0402 [SMD]"]
  R3 = Resistor [tolerance=±5% resistance=220 package="0402 [SMD]"]
  D1 = Rectifier Diode 10A [part_number=P1000K]
  D2 = Schottky Diode [part_number=1N5817 package="Melf DO-213 AB [SMD]"]
  D3 = Schottky Diode [part_number=1N5817 package="Melf DO-213 AB [SMD]"]
  VALVE1 = Plastic Solenoid Valve
  VALVE2 = Plastic Solenoid Valve
  VALVE3 = Plastic Solenoid Valve

nets:
  N1: Part1.D12/MISO, R2.Pin_0
  N2: Part1.D13/SCK, R1.Pin_0
  N3: Part1.D6_PWM, R3.Pin_0
  N4: Part1.GND, Q1.EMITTER, Q2.EMITTER, Q3.EMITTER
  N5: Part1.VIN, D1.cathode, D2.cathode, D3.cathode, VALVE1.no_name_yet#2, VALVE2.no_name_yet#2, VALVE3.no_name_yet#2
  N6: Q1.BASE, R1.Pin_1
  N7: Q1.COLLECTOR, D1.anode, VALVE1.no_name_yet#1
  N8: Q2.BASE, R2.Pin_1
  N9: Q2.COLLECTOR, D2.anode, VALVE2.no_name_yet#1
  N10: Q3.BASE, R3.Pin_1
  N11: Q3.COLLECTOR, D3.anode, VALVE3.no_name_yet#1
